# Fritzing sketch SmacSchema (saved by Fritzing 0.9.2b)
breadboards: 1

parts:
  DHT2 = DHT11 Humitidy and Temperature Sensor
  R1 = Resistor [tolerance=±5% resistance=4.7k package="2512 [SMD]"]
  R3 = Resistor [tolerance=±5% resistance=470 package="2512 [SMD]"]
  Raspberry_Pi1 = Raspberry Pi 2
  R4 = Resistor [tolerance=±5% resistance=2.2k package=THT]
  R5 = Resistor [tolerance=±5% resistance=10k package=THT]
  KY-2 = Keyes Relay [package=THT]
  Q1 = NPN-Transistor [package="TO92 [THT]"]
  DHT3 = DHT11 Humitidy and Temperature Sensor
  R2 = Resistor [tolerance=±5% resistance=470 package="2512 [SMD]"]
  DHT4 = DHT11 Humitidy and Temperature Sensor

nets (from the breadboard view):
  VDD: DHT2.VDD, R1.Pin_1, R3.Pin_1, Raspberry_Pi1.3v3, DHT3.VDD, R2.Pin_1, DHT4.VDD
  N1: DHT2.DATA, Raspberry_Pi1.GIPO17, R2.Pin_0
  GND: DHT2.GND, Raspberry_Pi1.GND, R5.Pin_1, KY-2.ground, Q1.E, DHT3.GND, DHT4.GND
  N2: R1.Pin_0, Raspberry_Pi1.GIPO4, DHT4.DATA
  N3: R3.Pin_0, DHT3.DATA
  N4: Raspberry_Pi1.GIPO20, R4.Pin_1, R5.Pin_0
  N5: Raspberry_Pi1.5V, KY-2.power
  N6: R4.Pin_0, Q1.B
  N7: KY-2.signal, Q1.C

custom parts:
  DHT11 Humitidy and Temperature Sensor: DHT11 Humidity and Temperature Sensor
  Keyes Relay: The Keyes 5V relay module is suitable for SCM development, home appliance control. It uses a 5V~12V TIL control signal which can control DC / AC signal.
